# Fritzing sketch Final_circuit (saved by Fritzing 0.9.3b)
breadboards: 1

parts:
  B1 = Bolt WiFi Module [package=dip]
  R1 = Resistor [tolerance=±5% resistance=220 package="1206 [SMD]"]
  R2 = Resistor [tolerance=±5% resistance=220 package="1206 [SMD]"]
  R3 = Photocell (LDR) [package=THT]
  S1 = SWITCH-MOMENTARY-2 [package=tactile_switch_tall]

nets:
  N1: B1.pin1, R1.Pin_0, R2.Pin_0
  N2: B1.pin2, R2.Pin_1, S1.2
  N3: B1.pin10, R3.pin_0, S1.1
  N4: R1.Pin_1, R3.pin_1

notes:
  IoT Refrigerator

custom parts:
  Bolt WiFi Module: Bolt IoT platform gives you the capability to control your devices and collect data from IoT devices safely and securely no matter where you are. Get actionable insights by deploying machine learning algorithms with just a few clicks to detect anomalies as well as predict sensor values.
